// Logisim project LC-3-v2.circ as structural Verilog: 16 circuits, main circuit main
// RES
module main (
  input  Reset,
  output out_2,
  output out_3,
  output out_4,
  output out_5,
  output out_6,
  output out_7,
  output out_8,
  output [15:0] out_9,
  output [15:0] out_10,
  output [15:0] out_11,
  output [15:0] out_12,
  output [15:0] out_13,
  output [15:0] out_14,
  output [15:0] out_15,
  output [15:0] out_16,
  output [15:0] out_17,
  output halt,
  output [15:0] out_19,
  output [15:0] out_20,
  output [15:0] out_21,
  output [15:0] out_22
);

  wire decodeir_1_writereg, getcst_1_usecst, or16_1_out_2, or16_2_out_2, ramctrl_1_memload,
       ramctrl_1_memstore;
  wire [2:0] nzp_1_nzp;
  wire [15:0] alu_1_output, getcst_1_cst, RegIN, registres_1_out_sr1, registres_1_out_sr2;

  BiClock biclock_1 (.reset(Reset), .signal0(out_2), .signal1(out_3));
  RegPC regpc_1 (
    .IR(out_10), .PC(out_9), .H(out_3), .R(registres_1_out_sr1), .Reset(Reset), .Jump(out_4), .TestNZP(out_5));
  // Probe on out_9
  // Probe on out_11
  GetAddr getaddr_1 (.PC(out_9), .BaseR(registres_1_out_sr1), .IR(out_10), .Addr(out_11), .Fetch(out_2));
  // Probe on out_12
  LED led_1 (.in(out_6));
  RamCtrl ramctrl_1 (
    .Store(out_7), .Fetch(out_2), .Exec(out_3), .Load(out_6), .MemStore(ramctrl_1_memstore),
    .MemLoad(ramctrl_1_memload));
  LED led_2 (.in(out_7));
  // Probe on out_13
  RAM #(.addrWidth(16), .dataWidth(16), .bus("separate")) ram_1 (
    .addr(out_11), .din(out_12), .data(out_13), .str(ramctrl_1_memstore), .clk(ramctrl_1_memstore),
    .ld(ramctrl_1_memload));  // open: sel, clr
  Register #(.width(16), .trigger("falling")) RegIR (.D(out_13), .Q(out_10), .clk(out_2));  // open: en, clr
  DecodeIR decodeir_1 (.IR(out_10), .WriteReg(decodeir_1_writereg), .Store(out_7), .Jump(out_4), .Load(out_6));
  // Probe on out_10[11:9]
  // Probe on out_10[8:6]
  // Probe on out_10[2:0]
  // Probe on getcst_1_cst
  GetCst getcst_1 (.IR(out_10), .Cst(getcst_1_cst), .UseCst(getcst_1_usecst));
  // Probe on out_10[15:14]
  and and_1 (out_8, decodeir_1_writereg, out_3);
  Registres registres_1 (
    .SR1(out_10[8:6]), .IN(RegIN), .SR2(out_10[2:0]), .WriteReg(out_8), .DR_SR(out_10[11:9]),
    .OUT_SR1(registres_1_out_sr1), .OUT_SR2(registres_1_out_sr2), .OUT_SR(out_12), .R0(out_14), .R1(out_15),
    .R2(out_16), .R3(out_17), .R4(out_19), .R5(out_20), .R6(out_21), .R7(out_22));
  // Probe on registres_1_out_sr1
  ALU alu_1 (
    .UseCst(getcst_1_usecst), .e2(out_10[15:14]), .Input1(registres_1_out_sr1), .Input2(registres_1_out_sr2),
    .Cst(getcst_1_cst), .Output(alu_1_output));
  // Probe on RegIN
  // Probe on registres_1_out_sr2
  // Probe on alu_1_output
  NZP nzp_1 (.RES(RegIN), .IR(out_10), .WriteReg(out_8), .NZP(nzp_1_nzp), .TestNZP(out_5));
  // Probe on nzp_1_nzp
  Or16 or16_1 (.in_1(out_10), .out_2(or16_1_out_2));
  Or16 or16_2 (.in_1(out_9), .out_2(or16_2_out_2));
  // Probe on out_14
  // Probe on out_15
  // Probe on out_16
  // Probe on out_17
  // Probe on out_19
  // Probe on out_20
  // Probe on out_21
  // Probe on out_22
  and and_2 (halt, ~or16_1_out_2, or16_2_out_2);  // AND_Gate
  WriteVal writeval_1 (.Load(out_6), .ALURes(alu_1_output), .MemOUT(out_13), .PC(out_9), .RegIN(RegIN), .IR(out_10));
  // Probe on out_15

  // Other names for the same wires on the sheet: Addr[15:0] = out_11; Condition = out_5; Exec = out_3; Fetch = out_2;
  //   IR[15:0] = out_10; JumpInstr = out_4; Load = out_6; MemIN[15:0] = out_12; MemOUT[15:0] = out_13;
  //   PC[15:0] = out_9; R0[15:0] = out_14; R1[15:0] = out_15; R2[15:0] = out_16; R3[15:0] = out_17; R4[15:0] = out_19;
  //   R5[15:0] = out_20; R6[15:0] = out_21; R7[15:0] = out_22; Store = out_7; WriteReg = out_8

  // Notes on the sheet:
  //   R
  //   IR
  //   R
  //   IR
  //   RAM
  //   Traces (NE PAS MODIFIER)______________________________________________________________________________________________________
  //   GetOp
  //   Arret des traces au 1er NOP
endmodule

module ALU (
  input  [15:0] Input1,
  input  [15:0] Input2,
  input  [15:0] Cst,
  input  UseCst,
  input  [1:0] e2,
  output [15:0] Output
);

  wire [4:0] PopCount_out_2;
  wire [15:0] adder_1_out, And_out, multiplexer_1_out, Xor_et_Not_out;

  Multiplexer #(.width(16), .enable("false")) multiplexer_1 (
    .in0(Input2), .in1(Cst), .out(multiplexer_1_out), .sel(UseCst));
  Adder #(.width(16)) adder_1 (.a(multiplexer_1_out), .b(Input1), .out(adder_1_out));  // open: cin, cout
  assign And_out = Input1 & multiplexer_1_out;  // AND_Gate And, 16 bits wide
  Multiplexer #(.select(2), .width(16), .enable("false")) multiplexer_2 (
    .in0(adder_1_out), .in1(And_out), .in2(Xor_et_Not_out), .in3({{11{1'b0}}, PopCount_out_2}), .out(Output),
    .sel(e2));
  assign Xor_et_Not_out = Input1 ^ multiplexer_1_out;  // XOR_Gate Xor_et_Not, 16 bits wide
  PopCount PopCount (.Input(Input1), .out_2(PopCount_out_2));

  // Notes on the sheet:
  //   UseCst = 0 alors Utiliser SR2
  //   Input1 c'est l'adresse du registre SR1
  //   Sinon utiliser Imm5
  //   MUX qui permet de savoir quelle instruction on fait, ADD/AND/NOT/POPCOUNT/XOR
  //   Input2 c'est soit une constante Imm5 soit l'adresse du registre SR2
  //   Étant donné que xor et not ont le meme op code 
  //   MUX qui permet prends Input2 et Cst et qui permet de savoir si on utilise un SR2 ou un Imm5 en fonction de UseCst
endmodule

module BiClock (
  input  reset,
  output signal0,
  output signal1
);

  wire and_1_out, horloge_out, not_1_out, register_1_q;

  Clock horloge (.out(horloge_out));
  not not_1 (not_1_out, register_1_q);
  Register #(.width(1), .trigger("falling")) register_1 (
    .D(not_1_out), .Q(register_1_q), .clk(horloge_out), .clr(reset));  // open: en
  and and_1 (and_1_out, horloge_out, ~reset);  // AND_Gate
  and and_2 (signal0, ~register_1_q, and_1_out);  // AND_Gate
  and and_3 (signal1, register_1_q, and_1_out);

  // Notes on the sheet:
  //   Ce module divise une horloge en deux sous-horloges alternées
  //   Chronogrammes :
  //   horloge: 0101010101 signal0: 0100010001 signal1: 000100010
  //   registre 1-bit
  //   Enable
  //   select : 0 / 1
endmodule

module DecodeIR (
  input  [15:0] IR,
  output Store,
  output WriteReg,
  output Load,
  output Jump
);

  wire and_1_out, and_4_out, LEA_out;

  and LEA (LEA_out, IR[15], IR[14], IR[13], ~IR[12]);  // AND_Gate
  and and_1 (and_1_out, IR[13], IR[12]);
  and and_2 (Load, IR[13], ~IR[12]);  // AND_Gate
  and and_3 (Jump, IR[15], IR[14], ~IR[13], ~IR[12]);  // AND_Gate
  and and_4 (and_4_out, ~IR[13], IR[12]);  // AND_Gate
  and and_5 (Store, ~LEA_out, and_1_out);  // AND_Gate
  // Probe on and_4_out
  or or_1 (WriteReg, LEA_out, Load, and_4_out);

  // Notes on the sheet:
  //   Instruction modifiant les registres ?
  //   1110
  //   SR/STR 11
  //   LD/LDR 10
  //   JMP/JSR/JRR 00
  //   AND/NOT/XOR/ADD/POPCNT 01
endmodule

module GetAddr (
  input  [15:0] IR,
  input  Fetch,
  input  [15:0] PC,
  input  [15:0] BaseR,
  output [15:0] Addr
);

  wire or_1_out;
  wire [15:0] adder_1_out, adder_2_out, multiplexer_1_out, offset6_1_off6, offset9_1_off9;

  Offset9 offset9_1 (.IR(IR), .Off9(offset9_1_off9));
  Offset6 offset6_1 (.IR(IR), .Off6(offset6_1_off6));
  Adder #(.width(16)) adder_1 (.a(offset6_1_off6), .b(BaseR), .out(adder_1_out));  // open: cin, cout
  Adder #(.width(16)) adder_2 (.a(offset9_1_off9), .b(PC), .out(adder_2_out), .cin(1'b1));  // open: cout
  Multiplexer #(.width(16), .disabled(0), .enable("false")) multiplexer_1 (
    .in0(adder_2_out), .in1(adder_1_out), .out(multiplexer_1_out), .sel(IR[14]));
  or or_1 (or_1_out, ~IR[13], Fetch);  // OR_Gate
  Multiplexer #(.width(16), .disabled(0), .enable("false")) multiplexer_2 (
    .in0(multiplexer_1_out), .in1(PC), .out(Addr), .sel(or_1_out));

  // Notes on the sheet:
  //   PC+SEXT(Offset6)
  //   b14: label or BaseR?
  //   PC+SEXT(Offset9)
  //   b13: Load ou Store?
  //   Pourquoi ?
endmodule

module GetCst (
  input  [15:0] IR,
  output [15:0] Cst,
  output UseCst
);

  assign Cst = {{11{IR[4]}}, IR[4:0]};  // Bit_Extender bit_extender_1

  assign UseCst = IR[5];
endmodule

module NZP (
  input  [15:0] RES,
  input  WriteReg,
  input  [15:0] IR,
  output [2:0] NZP,
  output TestNZP
);

  wire \Négatif_out , Positifs_out, \Zéro_out ;
  wire [1:0] nor_1_out;

  Comparator #(.width(16)) comparator_1 (.a(RES), .b({16{1'b0}}), .eq(nor_1_out[1]));  // open: gt, lt
  nor nor_1 (nor_1_out[0], RES[15], nor_1_out[1]);
  Register #(.width(3)) register_1 (.D({RES[15], nor_1_out}), .Q(NZP), .clk(WriteReg));  // open: en, clr
  and \Négatif  (\Négatif_out , NZP[2], IR[11]);
  and \Zéro  (\Zéro_out , NZP[1], IR[10]);
  and Positifs (Positifs_out, NZP[0], IR[9]);
  or or_1 (TestNZP, \Négatif_out , \Zéro_out , Positifs_out);

  // Notes on the sheet:
  //   (Resultat du calcul courant)
  //   Sortie pour N
  //   Sortie pour P
  //   Sortie pour Z
  //   (Instruction courante)
  //   Marquage des conditions (avec ces 2 portes)
  //   Décide quand le registre a le droit de sauvegarder une nouvelle valeur
  //   si 1, instruction doit actualiser NZP
  //   Valeur actuelle du registre d'état NZP
  //   Test de saut : vrai siau moins un flag est vrai
endmodule

// Off6
module Offset6 (
  input  [15:0] IR,
  output [15:0] Off6
);

  assign Off6 = {{10{IR[5]}}, IR[5:0]};  // Bit_Extender bit_extender_1
endmodule

// Off9
module Offset9 (
  input  [15:0] IR,
  output [15:0] Off9
);

  assign Off9 = {{7{IR[8]}}, IR[8:0]};  // Bit_Extender bit_extender_1
endmodule

module Or16 (
  input  [15:0] in_1,
  output out_2
);

  wire [1:0] or_2_out;
  wire [7:0] or_1_out;

  assign or_1_out = in_1[7:0] | in_1[15:8];  // OR_Gate or_1, 8 bits wide
  assign or_2_out = or_1_out[1:0] | or_1_out[3:2] | or_1_out[5:4] | or_1_out[7:6];  // OR_Gate or_2, 2 bits wide
  or or_3 (out_2, or_2_out[0], or_2_out[1]);
endmodule

module RamCtrl (
  input  Exec,
  input  Fetch,
  input  Load,
  input  Store,
  output MemLoad,
  output MemStore
);

  wire and_1_out;

  and and_1 (and_1_out, Exec, Load);
  and and_2 (MemStore, Exec, Store);
  or or_1 (MemLoad, Fetch, and_1_out);
endmodule

module Registres (
  input  [2:0] SR1,
  input  [15:0] IN,
  input  [2:0] SR2,
  input  WriteReg,
  input  [2:0] DR_SR,
  output [15:0] R0,
  output [15:0] OUT_SR1,
  output [15:0] R1,
  output [15:0] R2,
  output [15:0] R3,
  output [15:0] OUT_SR2,
  output [15:0] R4,
  output [15:0] R5,
  output [15:0] OUT_SR,
  output [15:0] R6,
  output [15:0] R7
);

  wire decoder_1_out0, decoder_1_out1, decoder_1_out2, decoder_1_out3, decoder_1_out4, decoder_1_out5,
       decoder_1_out6, decoder_1_out7;

  Decoder #(.select(3), .disabled(0)) decoder_1 (
    .out0(decoder_1_out0), .out1(decoder_1_out1), .out2(decoder_1_out2), .out3(decoder_1_out3),
    .out4(decoder_1_out4), .out5(decoder_1_out5), .out6(decoder_1_out6), .out7(decoder_1_out7), .sel(DR_SR),
    .en(WriteReg));
  Register #(.width(16), .trigger("falling")) u_R0 (.D(IN), .Q(R0), .clk(decoder_1_out0));  // open: en, clr
  Register #(.width(16), .trigger("falling")) u_R1 (.D(IN), .Q(R1), .clk(decoder_1_out1));  // open: en, clr
  Register #(.width(16), .trigger("falling")) u_R2 (.D(IN), .Q(R2), .clk(decoder_1_out2));  // open: en, clr
  Register #(.width(16), .trigger("falling")) u_R3 (.D(IN), .Q(R3), .clk(decoder_1_out3));  // open: en, clr
  Register #(.width(16), .trigger("falling")) u_R4 (.D(IN), .Q(R4), .clk(decoder_1_out4));  // open: en, clr
  Register #(.width(16), .trigger("falling")) u_R5 (.D(IN), .Q(R5), .clk(decoder_1_out5));  // open: en, clr
  Register #(.width(16), .trigger("falling")) u_R6 (.D(IN), .Q(R6), .clk(decoder_1_out6));  // open: en, clr
  Register #(.width(16), .trigger("falling")) u_R7 (.D(IN), .Q(R7), .clk(decoder_1_out7));  // open: en, clr
  Multiplexer #(.select(3), .width(16), .enable("false")) multiplexer_1 (
    .in0(R0), .in1(R1), .in2(R2), .in3(R3), .in4(R4), .in5(R5), .in6(R6), .in7(R7), .out(OUT_SR1), .sel(SR1));
  Multiplexer #(.select(3), .width(16), .enable("false")) multiplexer_2 (
    .in0(R0), .in1(R1), .in2(R2), .in3(R3), .in4(R4), .in5(R5), .in6(R6), .in7(R7), .out(OUT_SR2), .sel(SR2));
  Multiplexer #(.select(3), .width(16), .enable("false")) multiplexer_3 (
    .in0(R0), .in1(R1), .in2(R2), .in3(R3), .in4(R4), .in5(R5), .in6(R6), .in7(R7), .out(OUT_SR), .sel(DR_SR));
endmodule

module RegPC (
  input  [15:0] IR,
  input  H,
  input  [15:0] R,
  input  Reset,
  input  Jump,
  input  TestNZP,
  output [15:0] PC
);

  wire and_1_out, and_2_out, and_3_out, and_4_out, BR_out, JSR_out, or_1_out;
  wire [15:0] adder_1_out, adder_2_out, bit_extender_1_out, multiplexer_1_out, multiplexer_2_out,
       multiplexer_3_out, offset9_1_off9;

  and BR (BR_out, ~IR[15], ~IR[14], ~IR[13], ~IR[12]);  // AND_Gate
  and JSR (JSR_out, ~IR[15], IR[14], ~IR[13], ~IR[12]);  // AND_Gate
  assign bit_extender_1_out = {{5{1'b0}}, IR[10:0]};  // Bit_Extender bit_extender_1
  and and_1 (and_1_out, IR[11], JSR_out);
  and and_2 (and_2_out, TestNZP, BR_out);
  Offset9 offset9_1 (.IR(IR), .Off9(offset9_1_off9));
  and and_3 (and_3_out, ~IR[11], JSR_out);  // AND_Gate
  or or_1 (or_1_out, Jump, JSR_out, and_2_out);
  Adder #(.width(16)) adder_1 (.a(PC), .b(16'h1), .out(adder_1_out));  // open: cin, cout
  Multiplexer #(.width(16), .disabled(0), .enable("false")) multiplexer_1 (
    .in0(offset9_1_off9), .in1(bit_extender_1_out), .out(multiplexer_1_out), .sel(and_1_out));
  and and_4 (and_4_out, and_3_out, JSR_out);
  Adder #(.width(16)) adder_2 (.a(adder_1_out), .b(multiplexer_1_out), .out(adder_2_out));  // open: cin, cout
  Multiplexer #(.width(16), .disabled(0), .enable("false")) multiplexer_2 (
    .in0(adder_2_out), .in1(R), .out(multiplexer_2_out), .sel(and_4_out));
  // Probe on multiplexer_3_out
  Multiplexer #(.width(16), .enable("false")) multiplexer_3 (
    .in0(adder_1_out), .in1(multiplexer_2_out), .out(multiplexer_3_out), .sel(or_1_out));
  Register #(.width(16), .trigger("falling")) u_PC (.D(multiplexer_3_out), .Q(PC), .clk(H), .clr(Reset));  // open: en

  // Notes on the sheet:
  //   pour BR
  //   pour JSR
  //   PC <- PC + 1
  //   BaseR ssi JMP ou JSRR
  //   PC+Off
  //   BaseR
  //   saut ssi JMP et (BR =>TestNZP)
  //   pas saut
  //   saut
endmodule

module Offset11 (
  input  [15:0] IR,
  output [15:0] SEXTOff11
);

  assign SEXTOff11 = {{5{1'b0}}, IR[10:0]};  // Bit_Extender bit_extender_1
endmodule

module WriteVal (
  input  [15:0] ALURes,
  input  [15:0] MemOUT,
  input  Load,
  input  [15:0] PC,
  input  [15:0] IR,
  output [15:0] RegIN
);

  wire JSR, LEA;
  wire [15:0] adder_1_out, adder_2_out, multiplexer_1_out, multiplexer_2_out, offset9_1_off9;

  Offset9 offset9_1 (.IR(IR), .Off9(offset9_1_off9));
  and and_1 (LEA, ~IR[12], IR[13], IR[14], IR[15]);  // AND_Gate
  and and_2 (JSR, ~IR[12], ~IR[13], IR[14], ~IR[15]);  // AND_Gate
  Adder #(.width(16)) adder_1 (.a(PC), .b(offset9_1_off9), .out(adder_1_out));  // open: cin, cout
  Multiplexer #(.width(16), .enable("false")) multiplexer_1 (
    .in0(ALURes), .in1(MemOUT), .out(multiplexer_1_out), .sel(Load));
  Adder #(.width(16)) adder_2 (.a(adder_1_out), .b(16'h1), .out(adder_2_out));  // open: cin, cout
  Multiplexer #(.width(16), .enable("false")) multiplexer_2 (
    .in0(multiplexer_1_out), .in1(adder_2_out), .out(multiplexer_2_out), .sel(LEA));
  Multiplexer #(.width(16), .enable("false")) multiplexer_3 (.in0(multiplexer_2_out), .in1(PC), .out(RegIN), .sel(JSR));

  // Notes on the sheet:
  //   Adresse d'instruction suivante
  //   Données lue dans la RAM
  //   Les calculs mathématiques
  //   Mémoire ou calcul
  //   PC + décalage +1
  //   RegIN = si JSR alors PC sinon si LEA alors PC+SEXT(Offset9) sinon si Load alors MemOUT sinon ALURes  
endmodule

module PopCount (
  input  [15:0] Input,
  output [4:0] out_2
);

  wire [1:0] adder_1_out, adder_2_out, adder_3_out, adder_4_out, adder_5_out, adder_6_out, adder_7_out,
       adder_8_out, adder_9_out, adder_10_out, adder_11_out, adder_12_out;
  wire [2:0] adder_13_out, adder_14_out;
  wire [2:2] adder_9_cout, adder_10_cout, adder_11_cout, adder_12_cout;
  wire [3:3] adder_13_cout, adder_14_cout;

  Adder #(.width(1)) adder_1 (.a(Input[0]), .b(Input[1]), .out(adder_1_out[0]), .cout(adder_1_out[1]));  // open: cin
  Adder #(.width(1)) adder_2 (.a(Input[2]), .b(Input[3]), .out(adder_2_out[0]), .cout(adder_2_out[1]));  // open: cin
  Adder #(.width(1)) adder_3 (.a(Input[4]), .b(Input[5]), .out(adder_3_out[0]), .cout(adder_3_out[1]));  // open: cin
  Adder #(.width(1)) adder_4 (.a(Input[6]), .b(Input[7]), .out(adder_4_out[0]), .cout(adder_4_out[1]));  // open: cin
  Adder #(.width(1)) adder_5 (.a(Input[8]), .b(Input[9]), .out(adder_5_out[0]), .cout(adder_5_out[1]));  // open: cin
  Adder #(.width(1)) adder_6 (.a(Input[10]), .b(Input[11]), .out(adder_6_out[0]), .cout(adder_6_out[1]));  // open: cin
  Adder #(.width(1)) adder_7 (.a(Input[12]), .b(Input[13]), .out(adder_7_out[0]), .cout(adder_7_out[1]));  // open: cin
  Adder #(.width(1)) adder_8 (.a(Input[14]), .b(Input[15]), .out(adder_8_out[0]), .cout(adder_8_out[1]));  // open: cin
  Adder #(.width(2)) adder_9 (
    .a(adder_1_out), .b(adder_2_out), .out(adder_9_out), .cout(adder_9_cout[2]));  // open: cin
  Adder #(.width(2)) adder_10 (
    .a(adder_3_out), .b(adder_4_out), .out(adder_10_out), .cout(adder_10_cout[2]));  // open: cin
  Adder #(.width(2)) adder_11 (
    .a(adder_5_out), .b(adder_6_out), .out(adder_11_out), .cout(adder_11_cout[2]));  // open: cin
  Adder #(.width(2)) adder_12 (
    .a(adder_7_out), .b(adder_8_out), .out(adder_12_out), .cout(adder_12_cout[2]));  // open: cin
  Adder #(.width(3)) adder_13 (
    .a({adder_9_cout[2], adder_9_out}), .b({adder_10_cout[2], adder_10_out}), .out(adder_13_out),
    .cout(adder_13_cout[3]));  // open: cin
  Adder #(.width(3)) adder_14 (
    .a({adder_11_cout[2], adder_11_out}), .b({adder_12_cout[2], adder_12_out}), .out(adder_14_out),
    .cout(adder_14_cout[3]));  // open: cin
  Adder #(.width(4)) adder_15 (
    .a({adder_13_cout[3], adder_13_out}), .b({adder_14_cout[3], adder_14_out}), .out(out_2[3:0]),
    .cout(out_2[4]));  // open: cin

  // Notes on the sheet:
  //   On fait la somme de tous les bits, puis la somme des retenues, afin d'avoir un nombre a la fin
endmodule
